// Logisim project Project1.circ as structural Verilog: 3 circuits, main circuit main
module main (
);

  wire Execute_we_2, Memory_we_2, registerfile_1_p2, WE_2_q, WE_q;
  wire [2:0] Control_q;
  wire [3:0] Op_2_q;
  wire [4:0] Execute_rd_2, Memory_rd_2, rd_2_q, rd_q, registerfile_1_p3, Sa_q;
  wire [31:0] A_q, B_q, C_q, Execute_c, Execute_pc_2, I_q, Memory_c_2, Memory_pc_2, mipsprogramrom_1_p1,
       mipsprogramrom_1_p2, PC_2_q, PC_3_q, registerfile_1_p1;

  // MIPSProgramROM mipsprogramrom_1: pin names not known; wires that end beside it: mipsprogramrom_1_p1, mipsprogramrom_1_p2
  Register #(.width(32)) Op (.D(mipsprogramrom_1_p2));  // open: en, Q, clk, clr
  Register #(.width(32)) PC (.D(mipsprogramrom_1_p1));  // open: en, Q, clk, clr
  // RegisterFile registerfile_1: pin names not known; wires that end beside it: registerfile_1_p1, registerfile_1_p2, registerfile_1_p3
  Register #(.width(32)) A (.Q(A_q));  // open: D, en, clk, clr
  Register #(.width(32)) B (.Q(B_q));  // open: D, en, clk, clr
  Register #(.width(16)) I (.Q(I_q[15:0]));  // open: D, en, clk, clr
  Register #(.width(5)) Sa (.Q(Sa_q));  // open: D, en, clk, clr
  Register #(.width(4)) Op_2 (.Q(Op_2_q));  // open: D, en, clk, clr
  Register #(.width(3)) Control (.Q(Control_q));  // open: D, en, clk, clr
  Register #(.width(5)) rd (.Q(rd_q));  // open: D, en, clk, clr
  Register #(.width(32)) PC_2 (.Q(PC_2_q));  // open: D, en, clk, clr
  Register #(.width(1)) WE (.Q(WE_q));  // open: D, en, clk, clr
  Execute Execute (
    .A(A_q), .B(B_q), .I(I_q), .Sa(Sa_q), .Op(Op_2_q), .Control(Control_q), .rd(rd_q), .PC(PC_2_q),
    .WE(WE_q), .C(Execute_c), .rd_2(Execute_rd_2), .PC_2(Execute_pc_2), .WE_2(Execute_we_2));
  Register #(.width(32)) C (.D(Execute_c), .Q(C_q));  // open: en, clk, clr
  Register #(.width(5)) rd_2 (.D(Execute_rd_2), .Q(rd_2_q));  // open: en, clk, clr
  Register #(.width(32)) PC_3 (.D(Execute_pc_2), .Q(PC_3_q));  // open: en, clk, clr
  Register #(.width(1)) WE_2 (.D(Execute_we_2), .Q(WE_2_q));  // open: en, clk, clr
  Memory Memory (
    .C(C_q), .rd(rd_2_q), .PC(PC_3_q), .WE(WE_2_q), .C_2(Memory_c_2), .rd_2(Memory_rd_2), .PC_2(Memory_pc_2),
    .WE_2(Memory_we_2));
  Register #(.width(32)) C_2 (.D(Memory_c_2), .Q(registerfile_1_p1));  // open: en, clk, clr
  Register #(.width(5)) rd_3 (.D(Memory_rd_2), .Q(registerfile_1_p3));  // open: en, clk, clr
  Register #(.width(32)) PC_4 (.D(Memory_pc_2), .Q(mipsprogramrom_1_p1));  // open: en, clk, clr
  Register #(.width(1)) WE_3 (.D(Memory_we_2), .Q(registerfile_1_p2));  // open: en, clk, clr
  // Pins of 16 and 32 bits meet at I_q

  // Notes on the sheet:
  //   Stage: Fetch
  //   Stage: Decode
  //   Stage: Writeback
  //   Stage: Execute
  //   Stage: Memory
  //   Stage: Writeback
endmodule

module Memory (
  input  [31:0] C,
  input  [4:0] rd,
  input  [31:0] PC,
  input  WE,
  output [31:0] C_2,
  output [4:0] rd_2,
  output [31:0] PC_2,
  output WE_2
);


  assign C_2 = C;
  assign PC_2 = PC;
  assign rd_2 = rd;
  assign WE_2 = WE;
endmodule

module Execute (
  input  [31:0] A,
  input  [31:0] B,
  input  [31:0] I,
  input  [4:0] Sa,
  input  [3:0] Op,
  input  [2:0] Control,
  input  [4:0] rd,
  input  [31:0] PC,
  input  WE,
  output [31:0] C,
  output [4:0] rd_2,
  output [31:0] PC_2,
  output WE_2
);

  wire comparator_1_lt, comparator_2_lt, multiplexer_2_out;
  wire [31:0] bit_extender_1_out, mips_alu_1_p5, multiplexer_1_out;

  Multiplexer #(.width(32), .enable("false")) multiplexer_1 (
    .in0(B), .in1(I), .out(multiplexer_1_out), .sel(Control[2]));
  // Mips_ALU mips_alu_1: pin names not known; wires that end beside it: A, multiplexer_1_out, Op, Sa, mips_alu_1_p5
  Comparator #(.width(32)) comparator_1 (.a(A), .b(multiplexer_1_out), .lt(comparator_1_lt));  // open: gt, eq
  Comparator #(.width(32), .mode("unsigned")) comparator_2 (
    .a(A), .b(multiplexer_1_out), .lt(comparator_2_lt));  // open: gt, eq
  Multiplexer #(.enable("false")) multiplexer_2 (
    .in0(comparator_1_lt), .in1(comparator_2_lt), .out(multiplexer_2_out), .sel(Control[0]));
  assign bit_extender_1_out = {{31{1'b0}}, multiplexer_2_out};  // Bit_Extender bit_extender_1
  Multiplexer #(.width(32), .enable("false")) multiplexer_3 (
    .in0(bit_extender_1_out), .in1(mips_alu_1_p5), .out(C), .sel(Control[1]));

  assign PC_2 = PC;
  assign rd_2 = rd;
  assign WE_2 = WE;
endmodule
